# Fritzing sketch Untitled Sketch (saved by Fritzing 0.9.10b)
breadboards: 1

parts:
  부품1 = Arduino Mega 2560 (Rev3)
  HC-SR04_Sensor_1 = HC-SR04 Ultrasonic Distance Sensor

nets:
  5V: 부품1.5V, HC-SR04_Sensor_1.VCC
  GND: 부품1.GND, HC-SR04_Sensor_1.GND
  N1: 부품1.D22, HC-SR04_Sensor_1.ECHO
  N2: 부품1.D23, HC-SR04_Sensor_1.TRIG
