# Fritzing sketch l298n-arduino (saved by Fritzing 0.9.10b)

parts:
  부품1 = Arduino Mega 2560 (Rev3)
  L298N1 = L298N DC motor driver
  VCC1 = Battery

nets:
  N1: 부품1.D10_PWM, L298N1.ENA
  N2: 부품1.D9_PWM, L298N1.IN1
  N3: 부품1.D8_PWM, L298N1.IN2
  5V: 부품1.5V, L298N1.5V
  GND: 부품1.GND, L298N1.GND, VCC1.-
  N4: L298N1.12V, VCC1.+

custom parts:
  L298N DC motor driver: 2x DC motor driver with 78M05 positive voltage regulator (7..35 V) L298N: max 46 V, 2 A Set 5 V Enable jumper to enable 5 V regultor (needed for the L298N) and +5 V output at screw terminal or supply external +5 V at screw terminal Set ENA and/or ENB to +5 V to enable motor permanently or supply ENA and/or ENB with PWM signal IN1 and IN2 set rotation directory for motor A (OUT1/OUT2) IN2 and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
